// Logisim project Chips.circ as structural Verilog: 5 circuits, main circuit TTTC
module TTTC (
  input  [1:0] vin,
  input  [1:0] hin,
  input  btn,
  output vout,
  output hout,
  output [3:0] L0,
  output [3:0] L1,
  output [3:0] L2,
  output [3:0] L3
);
endmodule

module BPC (
  input  H0,
  input  H1,
  input  H2,
  input  V0,
  input  V1,
  input  V2,
  input  reset,
  output ready,
  output [3:0] XY
);
endmodule

module SDR (
  input  [1:0] symID,
  input  [3:0] XY,
  input  clock,
  output [2:0] H0,
  output [2:0] H1,
  output [2:0] H2,
  output [2:0] V0,
  output [2:0] V1,
  output [2:0] V2
);
endmodule

module GSDD (
  input  [1:0] score,
  input  clock,
  output win,
  output lose,
  output draw
);
endmodule

module TTT (
  input  [1:0] hin,
  input  [1:0] vin,
  input  btn,
  output hout,
  output [3:0] L1,
  output [3:0] L2,
  output [3:0] L3,
  output [3:0] L4,
  output vout
);

  wire and_1_out, not_1_out;
  wire [1:0] register_1_q;
  wire [15:0] bitselector_1_out;

  and and_1 (and_1_out, hin[1], vin[1]);
  Register #(.width(2), .trigger("low")) register_1 (
    .D({vin[0], hin[0]}), .en(and_1_out), .Q(register_1_q), .clk(1'b0));  // open: clr
  not not_1 (not_1_out, register_1_q[1]);
  BitSelector #(.width(32), .group(16)) bitselector_1 (
    .in(32'h9429f99f), .out(bitselector_1_out), .sel(register_1_q[0]));
  BitSelector #(.width(32), .group(16)) bitselector_2 (
    .in({{16{1'b0}}, bitselector_1_out}), .out({L4, L3, L2, L1}), .sel(not_1_out));
  // Probe on {L4, L3, L2, L1}

  assign hout = btn;
  assign vout = btn;
endmodule
