// Logisim project Main.circ as structural Verilog: 1 circuit, main circuit Main
module Main (
);

  wire button_1_out, button_2_out, button_3_out, button_4_out, button_5_out, button_6_out, button_7_out,
       button_8_out, button_9_out, button_10_out, cdm_8_1_p2, cdm_8_1_p4, cdm_8_1_p5, cdm_8_1_p6, cdm_8_1_p7,
       cdm_8_1_p8, cdm_8_1_p9, cdm_8_1_p10, Cl, Code, data, decoder_1_out0, decoder_1_out1, decoder_3_out0,
       decoder_3_out1, gsdd_1_draw, gsdd_1_lose, gsdd_1_win, I_Osel, In_out_prime, IO_3_out, IO_4_out, mem,
       nand_1_out, not_1_out, not_2_out, RAM;
  wire [1:0] sdr_1_h0, sdr_1_h1, sdr_1_h2, sdr_1_v0, sdr_1_v1, sdr_1_v2;
  wire [2:2] tttc_1_hout, tttc_1_vout, tttc_2_hout, tttc_3_hout, tttc_4_vout, tttc_7_vout;
  wire [3:0] bpc_1_xy, I_Oadr, tttc_1_l0, tttc_1_l1, tttc_1_l2, tttc_1_l3, tttc_2_l0, tttc_2_l1, tttc_2_l2,
       tttc_2_l3, tttc_3_l0, tttc_3_l1, tttc_3_l2, tttc_3_l3, tttc_4_l0, tttc_4_l1, tttc_4_l2, tttc_4_l3,
       tttc_5_l0, tttc_5_l1, tttc_5_l2, tttc_5_l3, tttc_6_l0, tttc_6_l1, tttc_6_l2, tttc_6_l3, tttc_7_l0,
       tttc_7_l1, tttc_7_l2, tttc_7_l3, tttc_8_l0, tttc_8_l1, tttc_8_l2, tttc_8_l3, tttc_9_l0, tttc_9_l1,
       tttc_9_l2, tttc_9_l3;
  wire [7:0] cdm_8_1_p14, cdm_8_1_p15, I_Odat, random_1_out;
  wire [7:4] cdm_8_1_p13;
  wire [7:7] bpc_1_ready;

  // Probe on cdm_8_1_p4
  // Probe on cdm_8_1_p2
  Button button_1 (.out(button_1_out));
  Clock clock_1 (.out(Cl));
  and and_1 (I_Osel, not_1_out, Cl, data);
  GSDD gsdd_1 (.score(I_Odat[7:6]), .clock(decoder_1_out0), .win(gsdd_1_win), .lose(gsdd_1_lose), .draw(gsdd_1_draw));
  LED led_1 (.in(gsdd_1_win));
  // Probe on cdm_8_1_p7
  // Probe on cdm_8_1_p6
  // Probe on cdm_8_1_p5
  not not_1 (not_1_out, nand_1_out);
  and and_2 (RAM, nand_1_out, data);
  LED led_2 (.in(gsdd_1_draw));
  LED led_3 (.in(gsdd_1_lose));
  SDR sdr_1 (
    .symID(I_Odat[1:0]), .XY(I_Odat[5:2]), .Enable(decoder_1_out0), .H0(sdr_1_h0), .H1(sdr_1_h1),
    .H2(sdr_1_h2), .V0(sdr_1_v0), .V1(sdr_1_v1), .V2(sdr_1_v2));
  // Probe on cdm_8_1_p9
  // Probe on cdm_8_1_p8
  nand nand_1 (nand_1_out, cdm_8_1_p13[4], cdm_8_1_p13[5], cdm_8_1_p13[6], cdm_8_1_p13[7]);
  and IO_3 (IO_3_out, I_Osel, I_Oadr[0], I_Oadr[1], ~I_Oadr[2], ~I_Oadr[3]);  // AND_Gate
  // CdM_8 cdm_8_1: pin names not known; wires that end beside it: Cl, cdm_8_1_p2, button_1_out, cdm_8_1_p4, cdm_8_1_p5, cdm_8_1_p6, cdm_8_1_p7, cdm_8_1_p8, cdm_8_1_p9, cdm_8_1_p10, mem, In_out_prime, {cdm_8_1_p13, I_Oadr}, cdm_8_1_p14, cdm_8_1_p15
  Decoder #(.disabled(0)) decoder_1 (.out0(decoder_1_out0), .out1(decoder_1_out1), .sel(In_out_prime), .en(IO_3_out));
  TTTC tttc_1 (
    .vin(sdr_1_v0), .hin(sdr_1_h0), .btn(button_2_out), .vout(tttc_1_vout[2]), .hout(tttc_1_hout[2]),
    .L0(tttc_1_l0), .L1(tttc_1_l1), .L2(tttc_1_l2), .L3(tttc_1_l3));
  DotMatrix #(.inputtype("row"), .matrixcols(4), .matrixrows(4)) dotmatrix_1 (
    .row0(tttc_1_l0), .row1(tttc_1_l1), .row2(tttc_1_l2), .row3(tttc_1_l3));
  Button button_2 (.out(button_2_out));
  TTTC tttc_2 (
    .vin(sdr_1_v0), .hin(sdr_1_h1), .btn(button_3_out), .vout(tttc_1_vout[2]), .hout(tttc_2_hout[2]),
    .L0(tttc_2_l0), .L1(tttc_2_l1), .L2(tttc_2_l2), .L3(tttc_2_l3));
  DotMatrix #(.inputtype("row"), .matrixcols(4), .matrixrows(4)) dotmatrix_2 (
    .row0(tttc_2_l0), .row1(tttc_2_l1), .row2(tttc_2_l2), .row3(tttc_2_l3));
  Button button_3 (.out(button_3_out));
  TTTC tttc_3 (
    .vin(sdr_1_v0), .hin(sdr_1_h2), .btn(button_4_out), .vout(tttc_1_vout[2]), .hout(tttc_3_hout[2]),
    .L0(tttc_3_l0), .L1(tttc_3_l1), .L2(tttc_3_l2), .L3(tttc_3_l3));
  DotMatrix #(.inputtype("row"), .matrixcols(4), .matrixrows(4)) dotmatrix_3 (
    .row0(tttc_3_l0), .row1(tttc_3_l1), .row2(tttc_3_l2), .row3(tttc_3_l3));
  Button button_4 (.out(button_4_out));
  Decoder #(.disabled(0)) decoder_2 (.out0(Code), .out1(data), .sel(cdm_8_1_p10), .en(mem));
  assign I_Odat = not_2_out ? cdm_8_1_p14 : 8'bz;  // Controlled_Buffer controlled_buffer_1
  not not_2 (not_2_out, In_out_prime);
  assign cdm_8_1_p15 = In_out_prime ? I_Odat : 8'bz;  // Controlled_Buffer controlled_buffer_2
  TTTC tttc_4 (
    .vin(sdr_1_v1), .hin(sdr_1_h0), .btn(button_5_out), .vout(tttc_4_vout[2]), .hout(tttc_1_hout[2]),
    .L0(tttc_4_l0), .L1(tttc_4_l1), .L2(tttc_4_l2), .L3(tttc_4_l3));
  DotMatrix #(.inputtype("row"), .matrixcols(4), .matrixrows(4)) dotmatrix_4 (
    .row0(tttc_4_l0), .row1(tttc_4_l1), .row2(tttc_4_l2), .row3(tttc_4_l3));
  Button button_5 (.out(button_5_out));
  TTTC tttc_5 (
    .vin(sdr_1_v1), .hin(sdr_1_h1), .btn(button_6_out), .vout(tttc_4_vout[2]), .hout(tttc_2_hout[2]),
    .L0(tttc_5_l0), .L1(tttc_5_l1), .L2(tttc_5_l2), .L3(tttc_5_l3));
  DotMatrix #(.inputtype("row"), .matrixcols(4), .matrixrows(4)) dotmatrix_5 (
    .row0(tttc_5_l0), .row1(tttc_5_l1), .row2(tttc_5_l2), .row3(tttc_5_l3));
  Button button_6 (.out(button_6_out));
  TTTC tttc_6 (
    .vin(sdr_1_v1), .hin(sdr_1_h2), .btn(button_7_out), .vout(tttc_4_vout[2]), .hout(tttc_3_hout[2]),
    .L0(tttc_6_l0), .L1(tttc_6_l1), .L2(tttc_6_l2), .L3(tttc_6_l3));
  DotMatrix #(.inputtype("row"), .matrixcols(4), .matrixrows(4)) dotmatrix_6 (
    .row0(tttc_6_l0), .row1(tttc_6_l1), .row2(tttc_6_l2), .row3(tttc_6_l3));
  Button button_7 (.out(button_7_out));
  Pull_Resistor pull_resistor_1 (.node(I_Oadr[0]));
  Pull_Resistor pull_resistor_2 (.node(I_Oadr[1]));
  Pull_Resistor pull_resistor_3 (.node(I_Oadr[2]));
  Pull_Resistor pull_resistor_4 (.node(I_Oadr[3]));
  Pull_Resistor pull_resistor_5 (.node(cdm_8_1_p13[4]));
  Pull_Resistor pull_resistor_6 (.node(cdm_8_1_p13[5]));
  Pull_Resistor pull_resistor_7 (.node(cdm_8_1_p13[6]));
  Pull_Resistor pull_resistor_8 (.node(cdm_8_1_p13[7]));
  ROM rom_1 (.addr({cdm_8_1_p13, I_Oadr}), .data(I_Odat), .sel(Code));
  RAM ram_1 (.addr({cdm_8_1_p13, I_Oadr}), .data(I_Odat), .sel(RAM), .clk(Cl), .ld(In_out_prime));  // open: clr
  TTTC tttc_7 (
    .vin(sdr_1_v2), .hin(sdr_1_h0), .btn(button_8_out), .vout(tttc_7_vout[2]), .hout(tttc_1_hout[2]),
    .L0(tttc_7_l0), .L1(tttc_7_l1), .L2(tttc_7_l2), .L3(tttc_7_l3));
  DotMatrix #(.inputtype("row"), .matrixcols(4), .matrixrows(4)) dotmatrix_7 (
    .row0(tttc_7_l0), .row1(tttc_7_l1), .row2(tttc_7_l2), .row3(tttc_7_l3));
  Button button_8 (.out(button_8_out));
  TTTC tttc_8 (
    .vin(sdr_1_v2), .hin(sdr_1_h1), .btn(button_9_out), .vout(tttc_7_vout[2]), .hout(tttc_2_hout[2]),
    .L0(tttc_8_l0), .L1(tttc_8_l1), .L2(tttc_8_l2), .L3(tttc_8_l3));
  DotMatrix #(.inputtype("row"), .matrixcols(4), .matrixrows(4)) dotmatrix_8 (
    .row0(tttc_8_l0), .row1(tttc_8_l1), .row2(tttc_8_l2), .row3(tttc_8_l3));
  Button button_9 (.out(button_9_out));
  TTTC tttc_9 (
    .vin(sdr_1_v2), .hin(sdr_1_h2), .btn(button_10_out), .vout(tttc_7_vout[2]), .hout(tttc_3_hout[2]),
    .L0(tttc_9_l0), .L1(tttc_9_l1), .L2(tttc_9_l2), .L3(tttc_9_l3));
  DotMatrix #(.inputtype("row"), .matrixcols(4), .matrixrows(4)) dotmatrix_9 (
    .row0(tttc_9_l0), .row1(tttc_9_l1), .row2(tttc_9_l2), .row3(tttc_9_l3));
  Button button_10 (.out(button_10_out));
  and IO_4 (IO_4_out, I_Osel, ~I_Oadr[3], I_Oadr[2], ~I_Oadr[1], ~I_Oadr[0]);  // AND_Gate
  Random random_1 (.clk(decoder_3_out0), .next(decoder_3_out0), .out(random_1_out));  // open: clr
  Decoder #(.disabled(0)) decoder_3 (.out0(decoder_3_out0), .out1(decoder_3_out1), .sel(In_out_prime), .en(IO_4_out));
  assign I_Odat = decoder_3_out1 ? random_1_out : 8'bz;  // Controlled_Buffer controlled_buffer_3
  assign I_Odat = decoder_1_out1 ? {bpc_1_ready[7], 3'b000, bpc_1_xy} : 8'bz;  // Controlled_Buffer controlled_buffer_4
  BPC bpc_1 (
    .H0(tttc_1_hout[2]), .H1(tttc_2_hout[2]), .H2(tttc_3_hout[2]), .V0(tttc_1_vout[2]), .V1(tttc_4_vout[2]),
    .V2(tttc_7_vout[2]), .enable(decoder_1_out1), .ready(bpc_1_ready[7]), .XY(bpc_1_xy));

  // Other names for the same wires on the sheet: rd_wr_prime = In_out_prime

  // Notes on the sheet:
  //   contents of rom_1 (hex, n*v repeats v):
  //   cc f0 d2 2 d3 f3 bd d0 80 11 e3 6 b4 0 e1 6 d6 77 8a 8f ae d0 f bd 41 d0 8 71 e9 14 c3 d3 8e 17 fd
  //   c1 b5 5 c5 c7 e1 14 d6 77 8e 8b ee 6 d3 8e d0 9 88 e1 3f d6 64 5 e1 3e d0 c0 d7 fd b5 8f fe ba 8f 76
  //   e1 4e 5 e0 4e a e1 51 8f ee 34 fd b5 8f 5 e0 34 76 e1 34 89 e1 61 d0 40 ee 63 d0 80 d7 d1 8e d2 a 8a
  //   e1 6e d1 0 d7 f4 b0 8d 0 e1 75 d7 ee 68 a6 c1 c2 c3 d6 30 c7 c6 c5 95 95 11 19 c2 d2 f3 a9 c6 0 e0
  //   8d d4 d7 0 1 2 4 5 6 8 9 a 0 4 8 1 5 9 2 6 a 0 5 a 8 5 2
endmodule
